# Fritzing sketch TP1-1 (saved by Fritzing 0.9.3b)
breadboards: 1

parts:
  Composant1 = Arduino Uno (Rev3) - ICSP
  LED1 = smd LED [color="Green (565nm)" package="0603 [SMD]"]
  LED2 = smd LED [color="Red (633nm)" package="0603 [SMD]"]
  R1 = Resistor [tolerance=±5% resistance=220 package="2512 [SMD]"]
  R2 = Resistor [tolerance=±5% resistance=220 package="2512 [SMD]"]

nets:
  N1: Composant1.D12/MISO, R2.Pin_0
  N2: Composant1.D13/SCK, R1.Pin_0
  N3: Composant1.GND, LED1.cathode, LED2.cathode
  N4: LED1.anode, R2.Pin_1
  N5: LED2.anode, R1.Pin_1
