# Fritzing sketch TP1-9 (saved by Fritzing 0.9.3b)
breadboards: 1

parts:
  Composant1 = Arduino Uno (Rev3) - ICSP
  SG1 = Buzzer 12mm [package=buzzer-ccv]
  LED2 = smd LED [color="Green (560nm)" package="0603 [SMD]"]
  R1 = Resistor [tolerance=±5% resistance=220 package="2512 [SMD]"]
  R2 = Resistor [tolerance=±5% resistance=220 package="2512 [SMD]"]
  LED3 = smd LED [color="Red (633nm)" package="0603 [SMD]"]
  T1 = LM35 Temperature Sensor [package="TO92 [THT]"]

nets:
  N1: Composant1.A0, T1.Vout
  N2: Composant1.D9_PWM, SG1.2
  N3: Composant1.D12/MISO, R2.Pin_0
  N4: Composant1.D13/SCK, R1.Pin_0
  N5: Composant1.5V, T1.+Vs
  GND: Composant1.GND, SG1.1, LED2.cathode, LED3.cathode, T1.GND
  N6: LED2.anode, R2.Pin_1
  N7: R1.Pin_1, LED3.anode
